# Fritzing sketch Pylon (saved by Fritzing 0.9.3b)
circuit board: 4cm x 6cm
breadboards: 1

parts:
  Arduino = Arduino Nano (Rev3.0)
  R2 = Resistor [tolerance=±5% resistance=220 package=THT]
  R3 = Resistor [tolerance=±5% resistance=220 package=THT]
  LED = RGB LED (com. cathode, rgb) [package="5 mm [THT]"]
  R1 = Resistor [tolerance=±5% resistance=220 package=THT]
  HC12 = Header 6 [package=molex-1x6-ra]
  MPU6050 = MPU-6050 Board GY-521 [form="♀ (female)" package=THT]
  Set_Pin = Header 1 [package=1x01_offset]

nets:
  N1: Arduino.GND, LED.common_cathode, HC12.2, MPU6050.pin2
  N2: Arduino.D2, HC12.4
  N3: Arduino.D3, HC12.3
  N4: Arduino.D4, R1.Pin_0
  N5: Arduino.D5, R2.Pin_0
  N6: Arduino.D6, R3.Pin_0
  N7: Arduino.5V, HC12.1, MPU6050.pin1
  N8: Arduino.A5, MPU6050.pin3
  N9: Arduino.A4, MPU6050.pin4
  N10: R2.Pin_1, LED.green_anode
  N11: R3.Pin_1, LED.blue_anode
  N12: LED.red_anode, R1.Pin_1
  N13: HC12.5, Set_Pin.1

custom parts:
  MPU-6050 Board GY-521: Acelerometro y Giroscopio MPU-6050 Board GY-521
